# Fritzing sketch ARRC-Example01 (saved by Fritzing 0.9.3b)
breadboards: 1

parts:
  Part1 = Arduino Nano (Rev3.0)
  R1 = Resistor [tolerance=±5% resistance=10k package=THT]
  D1 = Rectifier Diode [part_number=1N4001 package="300 mil [THT]"]
  D2 = Rectifier Diode [part_number=1N4001 package="300 mil [THT]"]
  C1 = Electrolytic Capacitor [capacitance=10µF package="100 mil [THT, electrolytic]"]
  U1 = 3.5mm Audio Jack [package=audio-jack-3.5mm-smd]
  C2 = Tantalum Capacitor [capacitance=4.7µF package="100 mil [THT, tantalum]"]
  U2 = Optocoupler [package=THT]
  R2 = Resistor [tolerance=±5% resistance=1k package=THT]
  U3 = 3.5mm Audio Jack [package=audio-jack]
  R3 = Resistor [tolerance=±5% resistance=2.2k package=THT]

nets:
  N1: Part1.GND, D2.anode, U1.SLEEVE, R2.Pin_0
  N2: Part1.D3, U2.Pin_1
  N3: Part1.D4, C2.+, U2.Pin_5, U3.LEFT
  N4: Part1.A0, R1.Pin_1
  N5: R1.Pin_0, D1.cathode
  N6: D1.anode, D2.cathode, C1.-
  N7: C1.+, U1.RIGHT, C2.-
  N8: U2.Pin_2, R2.Pin_1
  N9: U2.Pin_4, R3.Pin_0
  N10: U3.SLEEVE, R3.Pin_1

notes:
  This schematic is examplary only!!!
  Altough it could be applied to most yaesu handheld radios but do examine the pinouts on accessory jacks!!!
